// Logisim project FinalProject.circ as structural Verilog
module DATAPATH (
  input  [7:0] INP,
  input  [1:0] in_2
);

  wire button_2_out;

  Adder adder_1 ();  // open: a, b, out, cin, cout
  // CONTROL control_1: pin names not known
  Multiplexer multiplexer_1 ();  // open: in0, in1, out, sel
  Clock clock_1 ();  // open: out
  Button button_1 ();  // open: out
  Multiplexer #(.select(2)) multiplexer_2 ();  // open: in0, in1, in2, in3, out, sel
  RAM #(.addrWidth(5), .clearpin("true"), .enables("line")) MEMORY (.clr(button_2_out));  // open: addr, we, clk, din, dout
  ROM #(.addrWidth(5)) INSTRUCTIONS ();  // open: addr, data
  Register #(.width(5)) register_1 ();  // open: D, en, Q, clk, clr
  Button button_2 (.out(button_2_out));
  ALU_CIRC alu_circ_1 ();
  Button button_3 ();  // open: out
  Register #(.width(5)) AC ();  // open: D, en, Q, clk, clr
endmodule

module CONTROL (
  input  [2:0] I,
  input  [4:0] CUR_AC,
  output [4:0] ADDR,
  output PC_SOURCE,
  output PC_SKIP,
  output AC_SOURCE,
  output ALU_SOURCE,
  output MEM_WRITE,
  output PC_WRITE,
  output AC_WRITE
);
endmodule
